// Digital circuit 4-bit-general-purpose-register.dig as structural Verilog
module _4_bit_general_purpose_register (
  input  [1:0] Address,
  input  clk,
  input  [3:0] Input,
  input  [1:0] CTRL,
  output [3:0] Output_BUS
);

  wire and_1_out, and_2_out, and_3_out, and_4_out, decoder_1_out_0, decoder_1_out_1, decoder_1_out_2,
       decoder_1_out_3;
  wire [3:0] R0_p4, R1_p4, R2_p4, R3_p4;

  Decoder #(.Selector_Bits(2)) decoder_1 (
    .sel(Address), .out_0(decoder_1_out_0), .out_1(decoder_1_out_1), .out_2(decoder_1_out_2),
    .out_3(decoder_1_out_3));
  and and_1 (and_1_out, clk, decoder_1_out_0);
  and and_2 (and_2_out, clk, decoder_1_out_1);
  and and_3 (and_3_out, clk, decoder_1_out_2);
  and and_4 (and_4_out, clk, decoder_1_out_3);
  // _4_Bit_instruction_register R0: pin names not known; wires that end beside it: and_1_out, Input, CTRL, R0_p4
  // _4_Bit_instruction_register R1: pin names not known; wires that end beside it: and_2_out, Input, CTRL, R1_p4
  // _4_Bit_instruction_register R2: pin names not known; wires that end beside it: and_3_out, Input, CTRL, R2_p4
  // _4_Bit_instruction_register R3: pin names not known; wires that end beside it: and_4_out, Input, CTRL, R3_p4
  Multiplexer #(.Selector_Bits(2), .Bits(4)) multiplexer_1 (
    .sel(Address), .in_0(R0_p4), .in_1(R1_p4), .in_2(R2_p4), .in_3(R3_p4), .out(Output_BUS));
endmodule
